# Fritzing sketch Untitled Sketch (saved by Fritzing 0.8.7b)
breadboards: 1

parts:
  Composant1 = Arduino Nano (Rev3.0)
  Composant2 = Adafruit_BMP280
  J1 = Piezo Speaker
  R1 = Trimmer Potentiometer [maximum_resistance=330Ω package=THT]
  R2 = Resistor [tolerance=±5% resistance=220 package="0603 [SMD]"]
  Composant3 = Standard LCD 16x2 white on blue [part_number=181]

nets:
  GND: Composant1.GND, Composant2.GND, J1.pin1, R1.leg2, Composant3.VSS, Composant3.R/W, Composant3.LED-
  N1: Composant1.D2, Composant3.DB7
  N2: Composant1.D3, Composant3.DB6
  N3: Composant1.D4, Composant3.DB5
  N4: Composant1.D5, Composant3.DB4
  N5: Composant1.D6, J1.pin2
  N6: Composant1.D11/MOSI, Composant3.E
  N7: Composant1.D12/MISO, Composant3.RS
  5V: Composant1.5V, Composant2.VIN, R1.leg1, R2.Pin_0, Composant3.VDD
  N8: Composant1.A5, Composant2.SCK/SCL
  N9: Composant1.A4, Composant2.SDI/SDA
  N10: R1.wiper, Composant3.V0
  N11: R2.Pin_1, Composant3.LED+

custom parts:
  Adafruit_BMP280: Bosch has stepped up their game with their new BMP280 sensor, an environmental sensor with temperature, barometric pressure that is the next generation upgrade to the BMP085/BMP180/BMP183. This sensor is great for all sorts of weather sensing and can even be used in both I2C and SPI! This precision sensor from Bosch is the best low-cost, precision sensing solution for measuring barometric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
  Standard LCD 16x2 white on blue: Standard HD44780 LCDs are useful for creating standalone projects. * 16 characters wide, 2 rows * White text on blue background * Connection port is 0.1" pitch, single row for easy breadboarding and wiring
